# Fritzing sketch ESP32_DFPlayerMini_BT (saved by Fritzing 0.9.6b)

parts:
  M1 = DOIT Esp32 DevKit v1 (30 pins long, 11 pins width) [part_number=ESP32S-PIN30]
  DFPlayer_Mini1 = DFPlayer MINI [package="DIP (Dual Inline) [THT]"]
  R1 = Resistor [tolerance=±5% resistance=1k package="2010 [SMD]"]

nets:
  N1: M1.GND, DFPlayer_Mini1.GND#6
  N2: M1.RX2, DFPlayer_Mini1.TX
  N3: M1.TX2, R1.Pin_0
  N4: M1.D19, DFPlayer_Mini1.BUSY
  VIN: M1.VIN, DFPlayer_Mini1.VCC
  N5: DFPlayer_Mini1.RX, R1.Pin_1

custom parts:
  DOIT Esp32 DevKit v1 (30 pins long, 11 pins width): The DOIT Esp32 DevKit v1 is one of the development board created by DOIT to evaluate the ESP-WROOM-32 module. It is based on the ESP32 microcontroller that boasts Wifi, Bluetooth, Ethernet and Low Power support all in a single chip. (vanepp) made breadboard work, adjusted pin numbering and labels and reduced size of schematic and cleaned up pcb. This chip is 30pins long (2 x15) and 11 pins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
  DFPlayer MINI: MP3 module by DFRobot.com for playing Music from an SD-Card. Supports WAV and MP3 files.
